# Fritzing sketch Circuit_Diagram (saved by Fritzing 0.9.2b)
breadboards: 1

parts:
  Part1 = Arduino Uno (Rev3)
  U1 = 74HC595 [package="DIP16 [THT]"]
  U2 = 74HC595 [package="DIP16 [THT]"]
  U3 = 74HC595 [package="DIP16 [THT]"]
  U4 = 74HC595 [package="DIP16 [THT]"]
  U5 = 74HC595 [package="DIP16 [THT]"]
  LED1 = RGB LED (com. anode, rbg) [package="5 mm [THT]"]
  LED2 = RGB LED (com. anode, rbg) [package="5 mm [THT]"]
  LED3 = RGB LED (com. anode, rbg) [package="5 mm [THT]"]
  LED4 = RGB LED (com. anode, rbg) [package="5 mm [THT]"]
  LED5 = RGB LED (com. anode, rbg) [package="5 mm [THT]"]
  LED6 = RGB LED (com. anode, rbg) [package="5 mm [THT]"]
  LED7 = RGB LED (com. anode, rbg) [package="5 mm [THT]"]
  LED8 = RGB LED (com. anode, rbg) [package="5 mm [THT]"]
  LED9 = RGB LED (com. anode, rbg) [package="5 mm [THT]"]
  LED10 = RGB LED (com. anode, rbg) [package="5 mm [THT]"]
  LED11 = RGB LED (com. anode, rbg) [package="5 mm [THT]"]
  LED12 = RGB LED (com. anode, rbg) [package="5 mm [THT]"]
  R1 = Resistor [tolerance=±5% resistance=200 package="0603 [SMD]"]

nets:
  N1: Part1.D8, U1.ST_CP, U2.ST_CP, U3.ST_CP, U4.ST_CP, U5.ST_CP
  N2: Part1.D11_PWM/MOSI, U1.DS
  N3: Part1.D13/SCK, U1.SH_CP, U2.SH_CP, U3.SH_CP, U4.SH_CP, U5.SH_CP
  VCC: Part1.5V, U1.MR, U1.VCC, U2.MR, U2.VCC, U3.MR, U3.VCC, U4.MR, U4.VCC, U5.MR, U5.VCC, R1.Pin_1
  GND: Part1.GND, U1.GND, U1.OE, U2.GND, U2.OE, U3.GND, U3.OE, U4.GND, U4.OE, U5.GND, U5.OE
  N4: U1.Q1, LED2.red_cathode
  N5: U1.Q2, LED3.red_cathode
  N6: U1.Q3, LED4.red_cathode
  N7: U1.Q4, LED5.red_cathode
  N8: U1.Q5, LED6.red_cathode
  N9: U1.Q6, LED7.red_cathode
  N10: U1.Q7, LED8.red_cathode
  N11: U1.Q7', U2.DS
  N12: U1.Q0, LED1.red_cathode
  N13: U2.Q1, LED10.red_cathode
  N14: U2.Q2, LED11.red_cathode
  N15: U2.Q3, LED12.red_cathode
  N16: U2.Q4, LED1.green_cathode
  N17: U2.Q5, LED2.green_cathode
  N18: U2.Q6, LED3.green_cathode
  N19: U2.Q7, LED4.green_cathode
  N20: U2.Q7', U3.DS
  N21: U2.Q0, LED9.red_cathode
  N22: U3.Q1, LED6.green_cathode
  N23: U3.Q2, LED7.green_cathode
  N24: U3.Q3, LED8.green_cathode
  N25: U3.Q4, LED9.green_cathode
  N26: U3.Q5, LED10.green_cathode
  N27: U3.Q6, LED11.green_cathode
  N28: U3.Q7, LED12.green_cathode
  N29: U3.Q7', U4.DS
  N30: U3.Q0, LED5.green_cathode
  N31: U4.Q1, LED2.blue_cathode
  N32: U4.Q2, LED3.blue_cathode
  N33: U4.Q3, LED4.blue_cathode
  N34: U4.Q4, LED5.blue_cathode
  N35: U4.Q5, LED6.blue_cathode
  N36: U4.Q6, LED7.blue_cathode
  N37: U4.Q7, LED8.blue_cathode
  N38: U4.Q7', U5.DS
  N39: U4.Q0, LED1.blue_cathode
  N40: U5.Q1, LED10.blue_cathode
  N41: U5.Q2, LED11.blue_cathode
  N42: U5.Q3, LED12.blue_cathode
  N43: U5.Q0, LED9.blue_cathode
  N44: LED1.common_anode, LED2.common_anode, LED3.common_anode, LED4.common_anode, LED5.common_anode, LED6.common_anode, LED7.common_anode, LED8.common_anode, LED9.common_anode, LED10.common_anode, LED11.common_anode, LED12.common_anode, R1.Pin_0
